# Fritzing sketch FritzingRP2040Sketch (saved by Fritzing 1.0.6)
circuit board: 7.5259cm x 14.3902cm

parts:
  LowerRotaryEnc = Rotary Encoder [package=THT]
  UpperRotaryEnc = Rotary Encoder [package=THT]
  UpperLitPower = Illuminated Pushbutton
  LowerLitPower = Illuminated Pushbutton
  UppI2CJumper = Header 4 [package=jst-4-pth]
  LowerI2CJumper = Header 4 [package=jst-4-pth]
  5VPowerJumper = Header 4 [package=jst-4-pth]
  RP2040 = Raspberry Pi Pico

nets:
  N1: LowerRotaryEnc.EncoderPinA, RP2040.pin_4
  GND: LowerRotaryEnc.EncoderPinC, LowerRotaryEnc.SwitchrPinD, UpperRotaryEnc.EncoderPinC, UpperRotaryEnc.SwitchrPinD, UpperLitPower.S-1, UpperLitPower.LED-, LowerLitPower.S-1, LowerLitPower.LED-, UppI2CJumper.1, LowerI2CJumper.1, RP2040.pin_3, RP2040.pin_18, RP2040.pin_23, RP2040.pin_28, RP2040.pin_38, RP2040.pin_42
  N2: LowerRotaryEnc.EncoderPinB, RP2040.pin_5
  N3: LowerRotaryEnc.SwitchPinE, RP2040.pin_6
  N4: UpperRotaryEnc.EncoderPinA, RP2040.pin_24
  N5: UpperRotaryEnc.EncoderPinB, RP2040.pin_25
  N6: UpperRotaryEnc.SwitchPinE, RP2040.pin_22
  N7: UpperLitPower.LED+, RP2040.pin_14
  N8: UpperLitPower.S-2, RP2040.pin_21
  N9: LowerLitPower.LED+, RP2040.pin_20
  N10: LowerLitPower.S-2, RP2040.pin_19
  N11: UppI2CJumper.2, RP2040.pin_26
  N12: UppI2CJumper.3, RP2040.pin_27
  N13: UppI2CJumper.4, RP2040.pin_29
  N14: LowerI2CJumper.2, RP2040.pin_31
  N15: LowerI2CJumper.3, RP2040.pin_32
  N16: LowerI2CJumper.4, RP2040.pin_34
  N17: 5VPowerJumper.4, RP2040.pin_40

notes:
  Pin List for RP2040
  MFD (upper):
  Rotary:
  A: GP18 (4 from bottom right)
  B: GP19 (5 up from bottom right)
  SW: GP17(second pin from bottom)
  Button:
  GP16
  LED:
  GP10 (Other side of board!)
  i2c0 (Wire.begin(20, 21):
  Sda: gp20(
  scl: gp21
  Int: gp22
  PFD:
  Rotary:
  A: GP2
  B: GP3
  SW: GP4
  Button:
  GP14
  LED:
  GP15
  i2c1: (Wire1.begin(26,27)
  SDA: gp26
  SCL: gp27
  Int: gp28

custom parts:
  Rotary Encoder: Rotary Encoder from ALPSec11e with switch.
  Raspberry Pi Pico: Raspberry Pi Pico. Based around the RP2040 microcontroller the Pico is a low cost microcontroller device bringing Raspberry Pi quality, cost, and easy of use to the microcontroller space. Jan 2021, Split part in to two versions: tht (this one) and SMD. This one will drill holes for a .1 in header in pcb to allow plugging in the module as well as providing pads to solder the module to the top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
